# Fritzing sketch Schematics (saved by Fritzing 1.0.6)

parts:
  J2 = Piezo Speaker
  Sensor1 = TTP223B Capacitive Touch Sensor Module
  Part1 = Barometric Pressure Sensor - BMP180 Breakout (GY-68)
  OLED_I2C1 = OLED 128x64 I2C Monochrome Display
  A1 = Waveshare rp2040-zero tht [package=THT]

nets:
  GND: J2.pin1, Sensor1.GND, Part1.GND, OLED_I2C1.GND, A1.Pin_2
  N1: J2.pin2, A1.Pin_7
  VCC: Sensor1.VCC, Part1.VCC, OLED_I2C1.VDD, A1.Pin_3
  N2: Sensor1.SIG, A1.Pin_6
  N3: Part1.SCL, OLED_I2C1.SCK, A1.Pin_4
  N4: Part1.SDA, OLED_I2C1.SDA, A1.Pin_5

custom parts:
  TTP223B Capacitive Touch Sensor Module: The TTP223B capacitive touch sensor module uses the TTP223B IC. The appropriate voltage is approximately 2 to 5.5 volts.
  Waveshare rp2040-zero tht: .RP2040-Zero, A Low-Cost, High-Performance Pico-Like MCU Board Based On Raspberry Pi Microcontroller RP2040. This varant is THT without the extra connections.
